// Digital circuit datapath.dig as structural Verilog
module datapath (
  input  clk,
  input  [7:0] d_rdat,
  input  en,
  input  cy_i,
  input  [1:0] \byte ,
  input  slt_i,
  input  rs_i,
  input  [29:0] instr,
  input  pc_cyi,
  output [7:0] d_adr,
  output [7:0] pc,
  output [7:0] res,
  output cy_o,
  output rs_o,
  output slt_o,
  output pc_cyo
);

  wire add_2_c_o, alt, comparator_1_eq, comparator_2_eq, comparator_3_eq, cy_it, en_ir, en_mar, en_pc,
       en_reg, LN, lsb, lt, ltu, msb, multiplexer_3_out, mux_cy, mux_func, mux_lhs, mux_pc, mux_res, mux_rhs,
       mux_sb, mux_sub, N, RN, rs_it, sub, V;
  wire [0:0] multiplexer_2_out;
  wire [1:0] mux_imm;
  wire [2:0] funct3, multiplexer_16_out;
  wire [3:0] multiplexer_2_out_2;
  wire [4:0] multiplexer_11_out, op, rd, rs1, rs2, ucode_d_2, upc_q;
  wire [6:0] add_2_s, funct7, multiplexer_12_out;
  wire [7:0] add_1_s, and_2_out, multiplexer_1_out, multiplexer_6_out, multiplexer_7_out, multiplexer_9_out,
       multiplexer_14_out, not_1_out, or_1_out, rf_da, rf_db, xor_1_out;
  wire [7:2] multiplexer_8_out;
  wire [10:0] ucode_d;
  wire [31:0] bitextender_1_out, bitextender_2_out, bitextender_3_out, multiplexer_10_out;

  Multiplexer #(.Bits(8)) multiplexer_1 (.sel(lsb), .in_0({8{1'b0}}), .in_1(8'h4), .out(multiplexer_1_out));
  Multiplexer #(.Bits(5)) multiplexer_2 (
    .sel(mux_sb), .in_0(rs2), .in_1(rd), .out({multiplexer_2_out_2, multiplexer_2_out[0]}));
  Add #(.Bits(8)) add_1 (.a(pc), .b(multiplexer_1_out), .c_i(pc_cyi), .s(add_1_s), .c_o(pc_cyo));
  RegisterFile #(.AddrBits(5), .Bits(8)) rf (
    .Din(res), .we(en_reg), .Rw(rd), .C(clk), .Ra(rs1), .Rb(rs2), .Da(rf_da), .Db(rf_db));
  Multiplexer multiplexer_3 (.sel(alt), .in_0(1'b0), .in_1(LN), .out(multiplexer_3_out));
  Register #(.Bits(30)) ir (
    .D(instr), .C(clk), .en(en_ir), .Q({funct7[6], alt, funct7[4:0], rs2, rs1, funct3, rd, op}));
  Multiplexer multiplexer_4 (.sel(msb), .in_0(rs_i), .in_1(multiplexer_3_out), .out(rs_it));
  Multiplexer multiplexer_5 (.sel(lsb), .in_0(cy_i), .in_1(sub), .out(cy_it));
  Multiplexer #(.Bits(8)) multiplexer_6 (.sel(mux_pc), .in_0(add_1_s), .in_1(res), .out(multiplexer_6_out));
  BitExtender #(.inputBits(12), .outputBits(32)) bitextender_1 (
    .in({funct7[6], alt, funct7[4:0], multiplexer_2_out_2, multiplexer_2_out[0]}), .out(bitextender_1_out));
  BitExtender #(.inputBits(13), .outputBits(32)) bitextender_2 (
    .in({funct7[6], multiplexer_2_out[0], alt, funct7[4:0], multiplexer_2_out_2, 1'b0}),
    .out(bitextender_2_out));
  BitExtender #(.inputBits(21), .outputBits(32)) bitextender_3 (
    .in({funct7[6], rs1, funct3, multiplexer_2_out[0], alt, funct7[4:0], multiplexer_2_out_2, 1'b0}),
    .out(bitextender_3_out));
  Register #(.Bits(8)) u_pc (.D(multiplexer_6_out), .C(clk), .en(en_pc), .Q(pc));
  Multiplexer #(.Bits(8), .Selector_Bits(2)) multiplexer_7 (
    .sel(\byte ), .in_0(multiplexer_10_out[7:0]), .in_1(multiplexer_10_out[15:8]),
    .in_2(multiplexer_10_out[23:16]), .in_3(multiplexer_10_out[31:24]), .out(multiplexer_7_out));
  Multiplexer #(.Bits(8)) multiplexer_8 (.sel(mux_lhs), .in_0(pc), .in_1(rf_da), .out({LN, multiplexer_8_out, rs_o}));
  Multiplexer #(.Bits(8)) multiplexer_9 (
    .sel(mux_rhs), .in_0(rf_db), .in_1(multiplexer_7_out), .out(multiplexer_9_out));
  Multiplexer #(.Bits(32), .Selector_Bits(2)) multiplexer_10 (
    .sel(mux_imm), .in_0(bitextender_1_out),
    .in_1({funct7[6], alt, funct7[4:0], multiplexer_2_out_2, multiplexer_2_out[0], rs1, funct3, {12{1'b0}}}),
    .in_2(bitextender_2_out), .in_3(bitextender_3_out), .out(multiplexer_10_out));
  Comparator comparator_1 (.a(LN), .b(RN), .eq(comparator_1_eq));  // open: gt, lt
  Comparator comparator_2 (.a(LN), .b(N), .eq(comparator_2_eq));  // open: gt, lt
  Multiplexer #(.Bits(5)) multiplexer_11 (.sel(ucode_d[0]), .in_0(ucode_d_2), .in_1(op), .out(multiplexer_11_out));
  Multiplexer #(.Bits(8)) multiplexer_12 (
    .sel(sub), .in_0(multiplexer_9_out), .in_1(not_1_out), .out({RN, multiplexer_12_out}));
  assign not_1_out = ~multiplexer_9_out;  // Not not_1, 8 bits wide
  and and_1 (V, comparator_1_eq, ~comparator_2_eq);  // And
  Register #(.Bits(5)) upc (.D(multiplexer_11_out), .C(clk), .en(en), .Q(upc_q));
  ROM #(.AddrBits(5), .Bits(21)) ucode (
    .A(upc_q), .sel(1'b1),
    .D({mux_func, mux_imm, mux_sb, mux_sub, mux_cy, mux_res, mux_rhs, mux_lhs, mux_pc, ucode_d[10:6], ucode_d_2, ucode_d[0]}));
  Add #(.Bits(8)) add_2 (
    .a({LN, multiplexer_8_out, rs_o}), .b({RN, multiplexer_12_out}), .c_i(cy_it), .s({N, add_2_s}),
    .c_o(add_2_c_o));
  assign xor_1_out = multiplexer_9_out ^ {LN, multiplexer_8_out, rs_o};  // XOr xor_1, 8 bits wide
  assign or_1_out = multiplexer_9_out | {LN, multiplexer_8_out, rs_o};  // Or or_1, 8 bits wide
  assign and_2_out = multiplexer_9_out & {LN, multiplexer_8_out, rs_o};  // And and_2, 8 bits wide
  Multiplexer multiplexer_13 (.sel(mux_cy), .in_0(add_2_c_o), .in_1(LN), .out(cy_o));
  Comparator comparator_3 (.a(N), .b(V), .eq(comparator_3_eq));  // open: gt, lt
  not not_2 (lt, comparator_3_eq);
  not not_3 (ltu, cy_o);
  and and_3 (en_pc, ucode_d[6], en);
  and and_4 (en_reg, ucode_d[7], en);
  Multiplexer #(.Bits(8), .Selector_Bits(3)) multiplexer_14 (
    .sel(multiplexer_16_out), .in_0({N, add_2_s}), .in_1({multiplexer_8_out, rs_o, cy_it}),
    .in_2({{7{1'b0}}, slt_i}), .in_3({{7{1'b0}}, slt_i}), .in_4(xor_1_out),
    .in_5({rs_it, LN, multiplexer_8_out}), .in_6(or_1_out), .in_7(and_2_out), .out(multiplexer_14_out));
  Multiplexer #(.Bits(8)) multiplexer_15 (.sel(mux_res), .in_0(multiplexer_14_out), .in_1(d_rdat), .out(res));
  Multiplexer #(.Bits(3)) multiplexer_16 (.sel(mux_func), .in_0(3'b000), .in_1(funct3), .out(multiplexer_16_out));
  Register #(.Bits(8)) mar (.D({N, add_2_s}), .C(clk), .en(en_mar), .Q(d_adr));
  nor nor_1 (lsb, \byte [0], \byte [1]);
  and and_5 (msb, \byte [0], \byte [1]);
  and and_6 (en_mar, ucode_d[8], en);
  and and_7 (en_ir, ucode_d[9], en);
  Multiplexer multiplexer_17 (.sel(mux_sub), .in_0(ucode_d[10]), .in_1(alt), .out(sub));
  Multiplexer #(.Selector_Bits(2)) multiplexer_18 (
    .sel(multiplexer_16_out[1:0]), .in_0(1'b0), .in_1(lt), .in_2(ltu), .in_3(1'b0), .out(slt_o));

  // Other names for the same wires on the sheet: funct7[5] = alt; rs_ot = rs_o; byte_t[1:0] = \byte ; C = clk;
  //   cy_ot = cy_o; en_t = en; pc_cyit = pc_cyi; pc_cyot = pc_cyo; slt_it = slt_i
endmodule
