// Digital circuit dmem_fsm.dig as structural Verilog
module dmem_fsm (
  input  ack,
  input  req,
  input  stall,
  input  C,
  output cyc,
  output en,
  output stb
);

  wire and_1_out, and_2_out, and_3_out, and_4_out, and_5_out, and_7_out, not_1_out, not_2_out, not_3_out,
       or_2_out, or_3_out, Z_0_n, Z_1_n;

  not not_1 (not_1_out, ack);
  not not_2 (not_2_out, stall);
  not not_3 (not_3_out, Z_1_n);
  and and_1 (and_1_out, Z_0_n, not_2_out);
  and and_2 (and_2_out, not_3_out, req, not_2_out);
  and and_3 (and_3_out, Z_1_n, not_1_out);
  and and_4 (and_4_out, Z_0_n, stall);
  and and_5 (and_5_out, not_3_out, req, stall);
  or or_1 (cyc, Z_0_n, Z_1_n, req);
  and and_6 (en, Z_1_n, ack);
  and and_7 (and_7_out, not_3_out, req);
  or or_2 (or_2_out, and_1_out, and_2_out, and_3_out);
  or or_3 (or_3_out, and_4_out, and_5_out);
  or or_4 (stb, Z_0_n, and_7_out);
  D_FF u_Z_1_n (.D(or_2_out), .C(C), .Q(Z_1_n));  // open: nQ
  D_FF u_Z_0_n (.D(or_3_out), .C(C), .Q(Z_0_n));  // open: nQ
  // Probe dmem.fsm on {Z_1_n, Z_0_n}

  // Notes on the sheet:
  //   C: Hz: 2
endmodule
