// Digital circuit randomctrl.dig as structural Verilog
module randomctrl (
  input  [31:0] instr,
  input  en,
  output mux_lhs,
  output mux_rhs,
  output [1:0] mux_res,
  output en_reg
);

  wire op, or_1_out, or_3_out;

  and and_1 (op, instr[0], instr[1], ~instr[2], ~instr[3], instr[4], instr[5], ~instr[6]);  // And
  and and_2 (mux_rhs, instr[0], instr[1], ~instr[2], ~instr[3], instr[4], ~instr[5], ~instr[6]);  // And
  or or_1 (or_1_out, op, mux_rhs);
  or or_2 (mux_lhs, op, mux_rhs);
  or or_3 (or_3_out, op, mux_rhs);
  and and_3 (en_reg, en, or_1_out);
  Multiplexer #(.Bits(2)) multiplexer_1 (.sel(or_3_out), .in_0(2'b00), .in_1(2'b01), .out(mux_res));

  // Other names for the same wires on the sheet: en_t = en; opi = mux_rhs
endmodule
