// Digital circuit singlecycle.dig as structural Verilog
module singlecycle (
  input  clk,
  input  [31:0] d_rdat,
  input  en,
  input  [31:0] instr,
  input  ack,
  input  rst,
  output [19:0] d_adr,
  output [19:0] pc,
  output [31:0] d_wdat,
  output [3:0] d_msk,
  output [30:0] test,
  output [4:0] uop,
  output busy,
  output pass,
  output fail,
  output [31:0] ir
);

  wire add_1_c_o, and_2_out, and_6_out, boot, comparator_2_eq, comparator_3_eq, comparator_5_eq,
       comparator_6_eq, comparator_7_eq, cond, demultiplexer_5_out_0, en_ir, en_mar, en_pc, en_reg, en_str,
       inh, LN, lt, ltu, multiplexer_1_out, multiplexer_9_out, mux_ack, mux_addr, mux_alu, mux_func, mux_pc,
       mux_sb, mux_sub, N, next, not_3_out, not_4_out, not_5_out, rd_zero, RN, rs, sub, V, Z;
  wire [0:0] multiplexer_3_out, register_2_q;
  wire [1:0] bitextender_6_out, demultiplexer_4_out_0, demultiplexer_4_out_1, mux_br, mux_imm, mux_res;
  wire [2:0] multiplexer_17_out;
  wire [3:0] bitextender_7_out, demultiplexer_3_out_0, multiplexer_3_out_2;
  wire [4:0] uop_mapper_wrapper_1_uop;
  wire [7:0] dat0_d, dat1_d, dat2_d, dat3_d, demultiplexer_1_out_0, demultiplexer_1_out_1,
       demultiplexer_1_out_2, demultiplexer_1_out_3, multiplexer_4_out;
  wire [8:8] multiplexer_6_out;
  wire [15:0] multiplexer_5_out;
  wire [16:16] multiplexer_7_out;
  wire [19:0] address_s, multiplexer_2_out, multiplexer_10_out, plus_4_s, rf_da;
  wire [30:0] add_1_s, multiplexer_14_out;
  wire [30:20] rf_da_2;
  wire [31:0] and_3_out, bitextender_1_out, bitextender_2_out, bitextender_3_out, bitextender_4_out,
       bitextender_5_out, demultiplexer_2_out_0, multiplexer_11_out, multiplexer_12_out, multiplexer_13_out,
       multiplexer_16_out, not_1_out, or_1_out, or_2_out, or_4_out, prog_d, res_t, rf_db, sll_out, srl_a_out,
       xor_1_out;
  wire [31:1] ucode_d;
  wire [32:32] srl_a_out_2;

  ROM #(.AddrBits(16), .isProgramMemory("true"), .Bits(32)) prog (.A(multiplexer_2_out[17:2]), .sel(1'b1), .D(prog_d));
  Add #(.Bits(20)) plus_4 (.a(pc), .b(20'h4), .c_i(1'b0), .s(plus_4_s));  // open: c_o
  assign or_1_out = d_rdat | {dat3_d, dat2_d, dat1_d, dat0_d};  // Or or_1, 32 bits wide
  assign or_2_out = instr | prog_d;  // Or or_2, 32 bits wide
  Multiplexer multiplexer_1 (.sel(mux_ack), .in_0(next), .in_1(ack), .out(multiplexer_1_out));
  D_FF u_boot (.D(~rst), .C(clk), .nQ(boot));  // open: Q
  Multiplexer #(.Bits(20)) multiplexer_2 (.sel(mux_pc), .in_0(plus_4_s), .in_1(address_s), .out(multiplexer_2_out));
  Comparator #(.Bits(5)) comparator_1 (.a(ir[11:7]), .b({5{1'b0}}), .eq(rd_zero));  // open: gt, lt
  Multiplexer #(.Bits(5)) multiplexer_3 (
    .sel(mux_sb), .in_0(ir[24:20]), .in_1(ir[11:7]), .out({multiplexer_3_out_2, multiplexer_3_out[0]}));
  Register #(.Bits(32)) u_ir (.D(or_2_out), .C(clk), .en(en_ir), .Q(ir));
  Comparator comparator_2 (.a(LN), .b(RN), .eq(comparator_2_eq));  // open: gt, lt
  Multiplexer #(.Selector_Bits(2), .Bits(8)) multiplexer_4 (
    .sel(d_adr[1:0]), .in_0(or_1_out[7:0]), .in_1(or_1_out[15:8]), .in_2(or_1_out[23:16]),
    .in_3(or_1_out[31:24]), .out(multiplexer_4_out));
  Multiplexer #(.Bits(16)) multiplexer_5 (
    .sel(d_adr[1]), .in_0(or_1_out[15:0]), .in_1(or_1_out[31:16]), .out(multiplexer_5_out));
  uop_mapper_wrapper uop_mapper_wrapper_1 (.inst(ir), .useq(multiplexer_1_out), .uop(uop_mapper_wrapper_1_uop));
  Register register_1 (.D(mux_pc), .C(clk), .en(en), .Q(inh));
  Register #(.Bits(20)) u_pc (.D(multiplexer_2_out), .C(clk), .en(en_pc), .Q(pc));
  RegisterFile #(.AddrBits(5), .Bits(32)) rf (
    .Din(res_t), .we(en_reg), .Rw(ir[11:7]), .C(clk), .Ra(ir[19:15]), .Rb(ir[24:20]),
    .Da({LN, rf_da_2, rf_da}), .Db(rf_db));
  BitExtender #(.inputBits(12), .outputBits(32)) bitextender_1 (
    .in({ir[31:25], multiplexer_3_out_2, multiplexer_3_out[0]}), .out(bitextender_1_out));
  BitExtender #(.inputBits(13), .outputBits(32)) bitextender_2 (
    .in({ir[31], multiplexer_3_out[0], ir[30:25], multiplexer_3_out_2, 1'b0}), .out(bitextender_2_out));
  BitExtender #(.inputBits(21), .outputBits(32)) bitextender_3 (
    .in({ir[31], ir[19:12], multiplexer_3_out[0], ir[30:25], multiplexer_3_out_2, 1'b0}),
    .out(bitextender_3_out));
  Comparator comparator_3 (.a(LN), .b(N), .eq(comparator_3_eq));  // open: gt, lt
  Multiplexer multiplexer_6 (.sel(ir[14]), .in_0(multiplexer_4_out[7]), .in_1(1'b0), .out(multiplexer_6_out[8]));
  Multiplexer multiplexer_7 (.sel(ir[14]), .in_0(multiplexer_5_out[15]), .in_1(1'b0), .out(multiplexer_7_out[16]));
  Multiplexer #(.Bits(5)) multiplexer_8 (
    .sel(inh), .in_0(uop_mapper_wrapper_1_uop), .in_1(uop_mapper_wrapper_1_uop), .out(uop));
  Multiplexer #(.Selector_Bits(2)) multiplexer_9 (
    .sel(mux_br), .in_0(1'b0), .in_1(1'b1), .in_2(cond), .in_3(cond), .out(multiplexer_9_out));
  and and_1 (V, comparator_2_eq, ~comparator_3_eq);  // And
  BitExtender #(.inputBits(9), .outputBits(32)) bitextender_4 (
    .in({multiplexer_6_out[8], multiplexer_4_out}), .out(bitextender_4_out));
  BitExtender #(.inputBits(17), .outputBits(32)) bitextender_5 (
    .in({multiplexer_7_out[16], multiplexer_5_out}), .out(bitextender_5_out));
  Register useq (.D(busy), .C(clk), .en(and_2_out), .Q(next));
  and and_2 (and_2_out, en, ~inh);  // And
  or or_3 (mux_pc, multiplexer_9_out, boot);
  Multiplexer #(.Bits(20)) multiplexer_10 (.sel(mux_addr), .in_0(pc), .in_1(rf_da), .out(multiplexer_10_out));
  Multiplexer #(.Bits(32)) multiplexer_11 (
    .sel(mux_alu), .in_0(rf_db), .in_1(bitextender_1_out), .out(multiplexer_11_out));
  Multiplexer #(.Selector_Bits(2), .Bits(32)) multiplexer_12 (
    .sel(mux_imm), .in_0(bitextender_1_out),
    .in_1({ir[31:25], multiplexer_3_out_2, multiplexer_3_out[0], ir[19:12], {12{1'b0}}}),
    .in_2(bitextender_2_out), .in_3(bitextender_3_out), .out(multiplexer_12_out));
  Multiplexer #(.Selector_Bits(2), .Bits(32)) multiplexer_13 (
    .sel(ir[13:12]), .in_0(bitextender_4_out), .in_1(bitextender_5_out), .in_2(or_1_out), .in_3(or_1_out),
    .out(multiplexer_13_out));
  ROM #(.AddrBits(5), .Bits(32)) ucode (
    .A(uop), .sel(1'b1),
    .D({ucode_d[31:24], mux_res, mux_imm, mux_br, mux_sb, mux_sub, mux_ack, mux_func, mux_alu, mux_addr, ucode_d[11:1], busy}));
  Multiplexer #(.Bits(32)) multiplexer_14 (
    .sel(sub), .in_0(multiplexer_11_out), .in_1(not_1_out), .out({RN, multiplexer_14_out}));
  assign not_1_out = ~multiplexer_11_out;  // Not not_1, 32 bits wide
  BarrelShifter #(.Bits(32)) sll (.in({LN, rf_da_2, rf_da}), .shift(multiplexer_11_out[5:0]), .out(sll_out));
  assign xor_1_out = multiplexer_11_out ^ {LN, rf_da_2, rf_da};  // XOr xor_1, 32 bits wide
  BarrelShifter #(.Bits(33), .barrelShifterMode("arithmetic"), .direction("right")) srl_a (
    .in({rs, LN, rf_da_2, rf_da}), .shift(multiplexer_11_out[5:0]), .out({srl_a_out_2[32], srl_a_out}));
  assign or_4_out = multiplexer_11_out | {LN, rf_da_2, rf_da};  // Or or_4, 32 bits wide
  assign and_3_out = multiplexer_11_out & {LN, rf_da_2, rf_da};  // And and_3, 32 bits wide
  Demultiplexer #(.Selector_Bits(2), .Bits(8)) demultiplexer_1 (
    .sel(d_adr[1:0]), .in(rf_db[7:0]), .out_0(demultiplexer_1_out_0), .out_1(demultiplexer_1_out_1),
    .out_2(demultiplexer_1_out_2), .out_3(demultiplexer_1_out_3));
  Demultiplexer #(.Bits(16)) demultiplexer_2 (
    .sel(d_adr[1]), .in(rf_db[15:0]), .out_0(demultiplexer_2_out_0[15:0]),
    .out_1(demultiplexer_2_out_0[31:16]));
  Add #(.Bits(20)) address (
    .a(multiplexer_10_out), .b(multiplexer_12_out[19:0]), .c_i(1'b0), .s(address_s));  // open: c_o
  Add #(.Bits(32)) add_1 (
    .a({LN, rf_da_2, rf_da}), .b({RN, multiplexer_14_out}), .c_i(sub), .s({N, add_1_s}), .c_o(add_1_c_o));
  Comparator #(.Bits(32)) comparator_4 (.a({N, add_1_s}), .b({32{1'b0}}), .eq(Z));  // open: gt, lt
  not not_2 (ltu, add_1_c_o);
  Multiplexer #(.Selector_Bits(2), .Bits(32)) multiplexer_15 (
    .sel(ir[13:12]),
    .in_0({demultiplexer_1_out_3, demultiplexer_1_out_2, demultiplexer_1_out_1, demultiplexer_1_out_0}),
    .in_1(demultiplexer_2_out_0), .in_2(rf_db), .in_3(rf_db), .out(d_wdat));
  and and_4 (en_pc, ucode_d[6], en);
  and and_5 (en_reg, ucode_d[7], ~rd_zero, en);  // And
  Multiplexer #(.Selector_Bits(3), .Bits(32)) multiplexer_16 (
    .sel(multiplexer_17_out), .in_0({N, add_1_s}), .in_1(sll_out), .in_2({{31{1'b0}}, lt}),
    .in_3({{31{1'b0}}, ltu}), .in_4(xor_1_out), .in_5(srl_a_out), .in_6(or_4_out), .in_7(and_3_out),
    .out(multiplexer_16_out));
  Multiplexer #(.Bits(3)) multiplexer_17 (.sel(mux_func), .in_0(3'b000), .in_1(ir[14:12]), .out(multiplexer_17_out));
  Demultiplexer #(.Selector_Bits(2)) demultiplexer_3 (
    .sel(d_adr[1:0]), .in(en_str), .out_0(demultiplexer_3_out_0[0]), .out_1(demultiplexer_3_out_0[1]),
    .out_2(demultiplexer_3_out_0[2]), .out_3(demultiplexer_3_out_0[3]));
  BitExtender #(.inputBits(1), .outputBits(2)) bitextender_6 (.in(en_str), .out(bitextender_6_out));
  and and_6 (and_6_out, ~ir[7], ir[8], ~ir[9], ir[10], ~ir[11]);  // And
  Register #(.Bits(20)) mar (.D(address_s), .C(clk), .en(en_mar), .Q(d_adr));
  Demultiplexer #(.Bits(2)) demultiplexer_4 (
    .sel(d_adr[1]), .in(bitextender_6_out), .out_0(demultiplexer_4_out_0), .out_1(demultiplexer_4_out_1));
  BitExtender #(.inputBits(1), .outputBits(4)) bitextender_7 (.in(en_str), .out(bitextender_7_out));
  Register #(.Bits(32)) register_2 (.D(res_t), .C(clk), .en(and_6_out), .Q({test, register_2_q[0]}));
  Comparator #(.Bits(2)) comparator_5 (.a(pc[1:0]), .b(2'b00), .eq(comparator_5_eq));  // open: gt, lt
  Comparator #(.Bits(32)) comparator_6 (
    .a({test, register_2_q[0]}), .b({32{1'b0}}), .eq(comparator_6_eq));  // open: gt, lt
  Comparator #(.Bits(5)) comparator_7 (.a(uop), .b(5'b10010), .eq(comparator_7_eq));  // open: gt, lt
  Multiplexer #(.Selector_Bits(2), .Bits(32)) multiplexer_18 (
    .sel(mux_res), .in_0({{12{1'b0}}, plus_4_s}), .in_1(multiplexer_16_out), .in_2(multiplexer_12_out),
    .in_3(multiplexer_13_out), .out(res_t));
  xor xor_2 (lt, N, V);
  not not_3 (not_3_out, Z);
  not not_4 (not_4_out, lt);
  not not_5 (not_5_out, ltu);
  Multiplexer #(.Selector_Bits(2), .Bits(4)) multiplexer_19 (
    .sel(ir[13:12]), .in_0(demultiplexer_3_out_0), .in_1({demultiplexer_4_out_1, demultiplexer_4_out_0}),
    .in_2(bitextender_7_out), .in_3(bitextender_7_out), .out(d_msk));
  and and_7 (en_str, ucode_d[8], en);
  and and_8 (en_mar, ucode_d[9], en);
  and and_9 (en_ir, ucode_d[10], en);
  Multiplexer multiplexer_20 (.sel(mux_sub), .in_0(ucode_d[11]), .in_1(ir[30]), .out(sub));
  Demultiplexer demultiplexer_5 (
    .sel(comparator_6_eq), .in(comparator_7_eq), .out_0(demultiplexer_5_out_0), .out_1(pass));
  Multiplexer multiplexer_21 (.sel(ir[30]), .in_0(1'b0), .in_1(LN), .out(rs));
  Multiplexer #(.Selector_Bits(3)) multiplexer_22 (
    .sel(ir[14:12]), .in_0(Z), .in_1(not_3_out), .in_2(1'b0), .in_3(1'b0), .in_4(lt), .in_5(not_4_out),
    .in_6(ltu), .in_7(not_5_out), .out(cond));
  or or_5 (fail, ~comparator_5_eq, demultiplexer_5_out_0);  // Or
  BlockRAMDualPort #(.AddrBits(8), .Bits(8)) dat0 (
    .A(d_adr[9:2]), .Din(d_wdat[7:0]), .str(d_msk[0]), .C(clk), .D(dat0_d));
  BlockRAMDualPort #(.AddrBits(8), .Bits(8)) dat1 (
    .A(d_adr[9:2]), .Din(d_wdat[15:8]), .str(d_msk[1]), .C(clk), .D(dat1_d));
  BlockRAMDualPort #(.AddrBits(8), .Bits(8)) dat2 (
    .A(d_adr[9:2]), .Din(d_wdat[23:16]), .str(d_msk[2]), .C(clk), .D(dat2_d));
  BlockRAMDualPort #(.AddrBits(8), .Bits(8)) dat3 (
    .A(d_adr[9:2]), .Din(d_wdat[31:24]), .str(d_msk[3]), .C(clk), .D(dat3_d));

  // Other names for the same wires on the sheet: busy_t = busy; C = clk; algn[1:0] = d_adr[1:0]; en_t = en;
  //   rd[4:0] = ir[11:7]; funct3[2:0] = ir[14:12]; rs1[4:0] = ir[19:15]; rs2[4:0] = ir[24:20];
  //   funct7[6:0] = ir[31:25]; alt = ir[30]; pcalgn[1:0] = pc[1:0]

  // Notes on the sheet:
  //   en: default 1
  //   contents of prog (hex, n*v repeats v):
  //   200193,93,113,20a733,393,4a771a63,300193,100093,100113,20a733
  //   ,393,48771e63,400193,300093,700113,20a733,100393,48771263,500193
  //   ,700093,300113,20a733,393,46771663,600193,93,ffff8137,20a733,393
  //   ,44771a63,700193,800000b7,113,20a733,100393,42771e63,800193,800000b7
  //   ,ffff8137,20a733,100393,42771263,900193,93,8137,fff10113,20a733
  //   ,100393,40771463,a00193,800000b7,fff08093,113,20a733,393,3e771663
  //   ,b00193,800000b7,fff08093,8137,fff10113,20a733,393,3c771663,c00193
  //   ,800000b7,8137,fff10113,20a733,100393,3a771863,d00193,800000b7
  //   ,fff08093,ffff8137,20a733,393,38771a63,e00193,93,fff00113,20a733
  //   ,393,36771e63,f00193,fff00093,100113,20a733,100393,36771263,1000193
  //   ,fff00093,fff00113,20a733,393,34771663,1100193,e00093,d00113,20a0b3
  //   ,393,32709a63,1200193,b00093,d00113,20a133,100393,30711e63,1300193
  //   ,d00093,10a0b3,393,30709463,1400193,213,b00093,d00113,20a733,70313
  //   ,120213,200293,fe5214e3,100393,2c731e63,1500193,213,e00093,d00113
  //   ,20a733,13,70313,120213,200293,fe5212e3,393,2a731663,1600193,213
  //   ,c00093,d00113,20a733,13,13,70313,120213,200293,fe5210e3,100393
  //   ,26731c63,1700193,213,e00093,d00113,20a733,120213,200293,fe5216e3
  //   ,393,24771863,1800193,213,b00093,d00113,13,20a733,120213,200293
  //   ,fe5214e3,100393,22771263,1900193,213,f00093,d00113,13,13,20a733
  //   ,120213,200293,fe5212e3,393,1e771a63,1a00193,213,a00093,13,d00113
  //   ,20a733,120213,200293,fe5214e3,100393,1c771463,1b00193,213,1000093
  //   ,13,d00113,13,20a733,120213,200293,fe5212e3,393,18771c63,1c00193
  //   ,213,900093,13,13,d00113,20a733,120213,200293,fe5212e3,100393
  //   ,16771463,1d00193,213,d00113,1100093,20a733,120213,200293,fe5216e3
  //   ,393,14771063,1e00193,213,d00113,800093,13,20a733,120213,200293
  //   ,fe5214e3,100393,10771a63,1f00193,213,d00113,1200093,13,13,20a733
  //   ,120213,200293,fe5212e3,393,e771263,2000193,213,d00113,13,700093
  //   ,20a733,120213,200293,fe5214e3,100393,a771c63,2100193,213,d00113
  //   ,13,1300093,13,20a733,120213,200293,fe5212e3,393,8771463,2200193
  //   ,213,d00113,13,13,600093,20a733,120213,200293,fe5212e3,100393
  //   ,4771c63,2300193,fff00093,102133,393,4711263,2400193,fff00093
  //   ,a133,100393,2711863,2500193,20b3,393,2709063,2600193,1000093
  //   ,1e00113,20a033,393,701463,2301063,ff0000f,18063,119193,11e193
  //   ,5d00893,18513,73,ff0000f,100193,5d00893,513,73,c0001073
  //   contents of ucode (hex, n*v repeats v):
  //   401,4144c0,404cc0,4144c0,1,1,1,4064c0,406cc0,4064c0,2a0c40,1,1
  //   ,9004c0,4*1,440,7*1
endmodule
