// Digital circuit uop_mapper.dig as structural Verilog
module uop_mapper (
  input  i28,
  input  i25,
  input  i20,
  input  i14,
  input  i13,
  input  i12,
  input  i6,
  input  i5,
  input  i4,
  input  i3,
  input  i2,
  input  iack,
  output o0,
  output o1,
  output o2,
  output o3,
  output o4
);

  wire and_1_out, and_2_out, and_3_out, and_4_out, and_5_out, and_6_out, and_7_out, and_8_out, and_9_out,
       and_10_out, and_11_out, and_12_out, and_13_out, and_14_out, and_15_out, and_16_out, and_17_out,
       and_18_out, and_19_out, and_20_out, and_21_out, and_22_out, and_23_out, and_24_out, and_25_out,
       and_26_out, and_27_out, and_28_out, and_29_out, and_30_out, and_31_out, and_32_out, and_33_out,
       and_34_out, and_35_out, and_36_out, and_37_out, and_38_out, and_39_out, and_40_out, and_41_out,
       and_42_out, and_43_out, and_44_out, and_45_out, and_46_out, and_47_out, and_48_out, not_1_out,
       not_2_out, not_3_out, not_4_out, not_5_out, not_6_out, not_7_out, not_8_out, not_9_out, not_10_out,
       not_11_out;

  not not_1 (not_1_out, i28);
  not not_2 (not_2_out, i25);
  not not_3 (not_3_out, i14);
  not not_4 (not_4_out, i13);
  not not_5 (not_5_out, i12);
  not not_6 (not_6_out, i6);
  not not_7 (not_7_out, i5);
  not not_8 (not_8_out, i4);
  not not_9 (not_9_out, i3);
  not not_10 (not_10_out, i2);
  not not_11 (not_11_out, iack);
  and and_1 (and_1_out, i12, not_10_out, not_9_out, i4, i5, i6);
  and and_2 (and_2_out, i13, not_10_out, not_9_out, i4, i5, i6);
  and and_3 (and_3_out, not_3_out, not_10_out, not_2_out, not_9_out, i4, i5, i6);
  and and_4 (and_4_out, not_3_out, not_10_out, not_1_out, not_9_out, i4, i5, i6);
  and and_5 (and_5_out, not_10_out, not_9_out, not_8_out, not_6_out, iack);
  and and_6 (and_6_out, i2, i3, not_8_out, not_7_out, not_6_out);
  and and_7 (and_7_out, not_10_out, not_9_out, not_8_out, i5, not_6_out);
  and and_8 (and_8_out, i12, not_4_out, not_2_out, not_9_out, i4, not_7_out, not_6_out);
  and and_9 (and_9_out, i12, not_10_out, not_9_out, i4, i5, i6);
  and and_10 (and_10_out, i13, not_10_out, not_9_out, i4, i5, i6);
  and and_11 (and_11_out, i13, not_3_out, not_9_out, i4, not_7_out, not_6_out);
  and and_12 (and_12_out, not_10_out, not_9_out, not_8_out, not_7_out, not_6_out, not_11_out);
  and and_13 (and_13_out, i2, not_9_out, i4, not_6_out);
  and and_14 (and_14_out, i2, not_8_out, i5, i6);
  and and_15 (and_15_out, not_9_out, not_8_out, i5, i6, not_11_out);
  and and_16 (and_16_out, not_5_out, not_4_out, not_3_out, not_10_out, not_2_out, not_9_out, i4, i5, i6);
  and and_17 (and_17_out, not_5_out, not_4_out, not_3_out, not_10_out, not_1_out, not_9_out, i4, i5, i6);
  and and_18 (and_18_out, not_5_out, not_4_out, not_9_out, i4, not_7_out, not_6_out);
  and and_19 (and_19_out, i13, i14, not_9_out, i4, not_7_out, not_6_out);
  and and_20 (and_20_out, not_10_out, not_9_out, not_8_out, not_7_out, not_6_out, not_11_out);
  and and_21 (and_21_out, i2, not_9_out, not_8_out, i5, i6);
  and and_22 (and_22_out, i2, not_9_out, i4, not_6_out);
  and and_23 (and_23_out, i25, not_9_out, i4, i5, not_6_out);
  and and_24 (and_24_out, not_5_out, not_4_out, not_3_out, not_10_out, not_2_out, i28, not_9_out, i4, i5, i6);
  and and_25 (and_25_out, i12, not_4_out, not_10_out, not_2_out, not_9_out, i4, i5, not_6_out);
  and and_26 (and_26_out, i12, i13, not_10_out, not_9_out, i4, i5, i6);
  and and_27 (and_27_out, not_5_out, not_4_out, not_9_out, i4, not_7_out, not_6_out);
  and and_28 (and_28_out, i13, not_3_out, not_10_out, not_2_out, not_9_out, i4, i5, not_6_out);
  and and_29 (and_29_out, i13, i14, not_10_out, i25, not_9_out, i4, not_6_out);
  and and_30 (and_30_out, i13, i14, not_9_out, i4, not_7_out, not_6_out);
  and and_31 (and_31_out, not_10_out, not_9_out, not_8_out, not_7_out, not_6_out, not_11_out);
  and and_32 (and_32_out, not_10_out, not_9_out, not_8_out, i5, not_6_out, iack);
  and and_33 (and_33_out, not_10_out, not_9_out, not_8_out, i5, i6, not_11_out);
  and and_34 (and_34_out, i2, i3, not_8_out, not_7_out, not_6_out);
  and and_35 (and_35_out, i2, not_9_out, i4, not_7_out, not_6_out);
  and and_36 (and_36_out, i2, i3, not_8_out, i5, i6);
  and and_37 (and_37_out, not_5_out, not_3_out, not_10_out, i20, not_2_out, not_9_out, i4, i5, i6);
  and and_38 (and_38_out, not_5_out, not_3_out, not_10_out, i20, not_1_out, not_9_out, i4, i5, i6);
  and and_39 (and_39_out, not_5_out, not_4_out, not_10_out, not_9_out, i4, not_7_out, not_6_out);
  and and_40 (and_40_out, not_5_out, i13, not_10_out, not_9_out, i4, i5, i6);
  and and_41 (and_41_out, i13, i14, not_10_out, not_9_out, i4, not_7_out, not_6_out);
  and and_42 (and_42_out, not_4_out, not_10_out, not_2_out, not_9_out, i4, not_6_out);
  and and_43 (and_43_out, not_4_out, i14, not_9_out, i4, i5, not_6_out);
  and and_44 (and_44_out, i14, not_10_out, not_2_out, not_9_out, i4, not_6_out);
  and and_45 (and_45_out, not_10_out, not_9_out, not_8_out, not_6_out, not_11_out);
  and and_46 (and_46_out, i2, i3, not_8_out, not_7_out, not_6_out);
  and and_47 (and_47_out, i2, not_9_out, i4, i5, not_6_out);
  and and_48 (and_48_out, i2, i3, not_8_out, i5, i6);
  or or_1 (o0, and_1_out, and_2_out, and_3_out, and_4_out, and_5_out, and_6_out, and_7_out);
  or or_2 (o1, and_8_out, and_9_out, and_10_out, and_11_out, and_12_out, and_13_out, and_14_out, and_15_out);
  or or_3 (o2, and_16_out, and_17_out, and_18_out, and_19_out, and_20_out, and_21_out, and_22_out, and_23_out);
  or or_4 (o3, and_24_out, and_25_out, and_26_out, and_27_out, and_28_out, and_29_out, and_30_out, and_31_out, and_32_out, and_33_out, and_34_out, and_35_out, and_36_out);
  or or_5 (o4, and_37_out, and_38_out, and_39_out, and_40_out, and_41_out, and_42_out, and_43_out, and_44_out, and_45_out, and_46_out, and_47_out, and_48_out);
endmodule
