// Digital circuit uop_mapper_wrapper.dig as structural Verilog
module uop_mapper_wrapper (
  input  [31:0] isnt,
  input  ack,
  output [4:0] uop
);

  wire and_1_out;
  wire [4:0] uop_mapper_1_o0;

  uop_mapper uop_mapper_1 (
    .i28(isnt[28]), .i25(isnt[25]), .i20(isnt[20]), .i14(isnt[14]), .i13(isnt[13]), .i12(isnt[12]),
    .i6(isnt[6]), .i5(isnt[5]), .i4(isnt[4]), .i3(isnt[3]), .i2(isnt[2]), .iack(ack),
    .o0(uop_mapper_1_o0[4]), .o1(uop_mapper_1_o0[3]), .o2(uop_mapper_1_o0[2]), .o3(uop_mapper_1_o0[1]),
    .o4(uop_mapper_1_o0[0]));
  and and_1 (and_1_out, isnt[1], isnt[0]);
  Multiplexer #(.Bits(5)) multiplexer_1 (.sel(and_1_out), .in_0({5{1'b0}}), .in_1(uop_mapper_1_o0), .out(uop));
endmodule
